// Logisim project PROGRAM5.circ as structural Verilog: 2 circuits, main circuit main
module main (
  input  in_1,
  input  in_2,
  input  in_3,
  output out_4
);

  wire and_1_out, not_1_out;

  not not_1 (not_1_out, in_1);
  and and_1 (and_1_out, not_1_out, in_2);
  or or_1 (out_4, in_3, and_1_out);
endmodule

module F_ABC (
  input  A,
  input  B,
  input  C,
  output F
);

  wire and_1_out, and_2_out, and_3_out, not_1_out, not_2_out, or_1_out;

  not not_1 (not_1_out, A);
  not not_2 (not_2_out, A);
  and and_1 (and_1_out, not_1_out, C);
  and and_2 (and_2_out, not_2_out, B);
  or or_1 (or_1_out, and_1_out, and_2_out);
  and and_3 (and_3_out, B, C);
  or or_2 (F, or_1_out, and_3_out);
endmodule
