// Logisim project PROGRAM6.circ as structural Verilog: 2 circuits, main circuit main
module main (
  input  in_1,
  input  in_2,
  input  in_3,
  input  in_4,
  output out_5
);

  wire and_1_out, and_2_out, not_1_out, not_2_out;

  not not_1 (not_1_out, in_2);
  not not_2 (not_2_out, in_4);
  and and_1 (and_1_out, in_2, in_4);
  and and_2 (and_2_out, not_1_out, not_2_out);
  or or_1 (out_5, and_2_out, and_1_out);
endmodule

module F_ABCD (
  input  A,
  input  B,
  input  C,
  input  D,
  output F
);

  wire and_1_out, and_2_out, not_1_out, not_2_out;

  not not_1 (not_1_out, B);
  and and_1 (and_1_out, not_1_out, not_2_out);
  not not_2 (not_2_out, D);
  and and_2 (and_2_out, B, D);
  or or_1 (F, and_1_out, and_2_out);
endmodule
