// Logisim project p12.circ as structural Verilog: 1 circuit, main circuit main
module main (
  input  in_1,
  input  [1:0] in_2,
  output out_3,
  output out_4,
  output out_5,
  output out_6
);

  Demultiplexer #(.select(2)) demultiplexer_1 (
    .out0(out_3), .out1(out_4), .out2(out_5), .out3(out_5), .in(in_1), .sel(in_2));  // open: en

  assign out_6 = out_5;
endmodule
