// Logisim project p19.circ as structural Verilog: 1 circuit, main circuit main
module main (
  input  in_1,
  input  in_2,
  input  in_3,
  input  [1:0] Operation,
  output Result,
  output C_out
);

  wire adder_1_out, and_1_out, or_1_out;

  Adder #(.width(1)) adder_1 (.a(in_1), .b(in_2), .out(adder_1_out), .cin(in_3), .cout(C_out));
  or or_1 (or_1_out, in_1, in_2);
  and and_1 (and_1_out, in_1, in_2);
  Multiplexer #(.select(2)) multiplexer_1 (
    .in0(or_1_out), .in1(and_1_out), .in2(adder_1_out), .out(Result), .sel(Operation));  // open: in3, en

  // Notes on the sheet:
  //   A
  //   B
  //   C-in
endmodule
